// Logisim project simulation.circ as structural Verilog
module main (
);

  wire addr_override_en, and_1_out, and_2_out, and_8_out, and_11_out, btn0, btn1, clear_screen, clk,
       clk_btn_out, clock_2_out, comparator_1_gt, comparator_2_lt, comparator_3_eq, comparator_3_lt,
       comparator_4_eq, comparator_5_gt, comparator_6_gt, comparator_7_gt, comparator_8_gt, comparator_9_eq,
       comparator_9_lt, comparator_11_eq, comparator_12_gt, comparator_13_gt, comparator_14_gt,
       comparator_15_gt, comparator_16_gt, cond_en, DE10_clk, decoder_1_out0, decoder_1_out1, decoder_1_out2,
       decoder_1_out3, decoder_2_out1, decoder_2_out2, decoder_2_out3, decoder_2_out4, decoder_2_out5,
       decoder_2_out6, decoder_2_out7, decoder_2_out10, decoder_2_out11, decoder_2_out12, decoder_2_out13,
       decoder_2_out14, decoder_2_out15, decoder_2_out16, decoder_2_out17, decoder_2_out18, decoder_2_out19,
       decoder_2_out30, decoder_2_out31, decoder_3_out3, decoder_3_out4, decoder_3_out5, decoder_3_out6,
       decoder_3_out7, decoder_3_out8, decoder_3_out9, decoder_3_out10, decoder_3_out11, decoder_3_out12,
       decoder_3_out13, decoder_3_out14, decoder_3_out15, decoder_3_out16, decoder_3_out17, decoder_3_out18,
       decoder_3_out19, decoder_3_out20, decoder_3_out21, decoder_3_out22, decoder_3_out23, decoder_3_out24,
       decoder_3_out25, decoder_3_out26, decoder_3_out27, decoder_3_out28, decoder_3_out29, decoder_3_out30,
       decoder_3_out31, decoder_4_out0, decoder_4_out1, decoder_4_out2, decoder_4_out3, decoder_4_out4,
       decoder_4_out5, decoder_4_out6, decoder_4_out7, decoder_4_out8, decoder_4_out9, decoder_4_out10,
       decoder_4_out11, decoder_4_out12, decoder_4_out13, decoder_4_out14, decoder_4_out15, decoder_4_out16,
       decoder_4_out17, decoder_4_out18, decoder_4_out19, decoder_4_out20, decoder_4_out21, decoder_4_out22,
       decoder_4_out30, decoder_4_out31, decoder_5_out0, decoder_5_out1, decoder_5_out2, decoder_6_out0,
       decoder_6_out1, decoder_6_out2, decoder_6_out3, decoder_6_out4, decoder_6_out5, decoder_7_out0,
       decoder_7_out1, decoder_7_out2, decoder_7_out3, draw_pixel, draw_sprite, F_write, freeze, halt,
       halted, mem_write, multiplexer_2_out, multiplexer_4_out, not_1_out, not_2_out, or_1_out, or_2_out,
       or_3_out, or_4_out, or_5_out, or_6_out, or_8_out, or_9_out, or_10_out, or_15_out, port_write,
       priority_encoder_1_gs, priority_encoder_2_gs, SP_en, SP_inc, tty_en, VGA_port_p3, write;
  wire [1:0] addr_mode, cond, vga_driver_1_hs, write_op_sel;
  wire [1:1] clocks_port_p3;
  wire [2:0] adder_3_out, instr_state, mode, multiplexer_5_out, multiplexer_6_out, write_sel;
  wire [2:2] subtractor_4_bout;
  wire [3:0] alu_1_flags_out, and_10_out, bit_extender_4_out, bit_extender_11_out, F, F_val,
       multiplexer_18_out, multiplexer_21_out, or_17_out, priority_encoder_1_out, priority_encoder_2_out,
       read_sel, vga_driver_1_vga_b, vga_driver_1_vga_g, vga_driver_1_vga_r;
  wire [3:2] adder_10_cout;
  wire [4:0] subtractor_5_out, subtractor_6_out, subtractor_7_out, subtractor_9_out;
  wire [5:0] bit_extender_7_out, bit_extender_9_out;
  wire [6:0] adder_6_out, multiplexer_10_out, pixel_q, subtractor_3_out;
  wire [7:0] A, adc_0, adc_1, adc_2, adc_3, adc_4, adc_5, adder_4_out, adder_8_out, adder_9_out,
       adder_10_out, alu_1_result, B, bit_extender_15_out, bit_extender_16_out, bit_extender_18_out,
       bit_extender_19_out, bit_extender_20_out, bit_extender_21_out, bit_extender_22_out,
       bit_extender_23_out, bit_extender_24_out, C0, C1, data, gfx_x, gfx_y, H, Instr_q, L, mem, mem_val,
       multiplexer_8_out, multiplexer_11_out, multiplexer_12_out, multiplexer_13_out, multiplexer_14_out,
       multiplexer_15_out, multiplexer_22_out, multiplexer_23_out, multiplexer_24_out, negator_1_out,
       port_in, Program_data, RAM_1_dout, random_1_out, shifter_1_out, SP, subtractor_1_out,
       subtractor_2_out, subtractor_4_out, subtractor_8_out;
  wire [7:2] instr;
  wire [8:0] bit_extender_2_out, bit_extender_3_out, multiplier_1_out;
  wire [9:0] and_3_out, and_12_out, and_13_out, bit_extender_5_out, leds, not_3_out, or_7_out, shifter_2_out,
       shifter_3_out, shifter_12_out, shifter_13_out, switches;
  wire [15:0] adder_1_out, adder_2_out, adder_5_out, addr_override, and_5_out, and_9_out, and_15_out,
       Arduino_in, Arduino_mode_q, Arduino_out_q, bit_extender_1_out, bit_extender_6_out,
       bit_extender_12_out, bit_extender_13_out, bit_extender_14_out, bit_extender_17_out, multiplexer_1_out,
       multiplexer_3_out, multiplexer_19_out, multiplexer_20_out, multiplier_2_out, not_5_out, not_7_out,
       or_13_out, or_14_out, PC, shifter_8_out, shifter_9_out, shifter_10_out, shifter_11_out, shifter_15_out;
  wire [23:0] Microcode_data, seven_seg;
  wire [35:0] and_4_out, and_6_out, and_14_out, bit_extender_8_out, bit_extender_10_out, GPIO_in,
       GPIO_mode_q, GPIO_out_q, not_4_out, not_6_out, or_11_out, or_12_out, shifter_4_out, shifter_5_out,
       shifter_6_out, shifter_7_out, shifter_14_out;

  Register #(.width(16)) u_PC (.D(multiplexer_1_out), .en(or_1_out), .clk(clk), .Q(PC));  // open: clr
  Multiplexer #(.enable("false"), .width(16)) multiplexer_1 (
    .in0(adder_2_out), .in1(multiplexer_3_out), .out(multiplexer_1_out), .sel(Microcode_data[21]));
  or or_1 (or_1_out, comparator_4_eq, Microcode_data[21], Microcode_data[20]);
  Multiplexer #(.enable("false"), .select(2)) multiplexer_2 (
    .in0(F[3]), .in1(F[2]), .in2(F[1]), .in3(F[0]), .out(multiplexer_2_out), .sel(cond));
  Comparator #(.mode("unsigned")) comparator_1 (.a(data), .b({8{1'b0}}), .gt(comparator_1_gt));  // open: eq, lt
  Comparator #(.mode("unsigned")) comparator_2 (.a(data), .b({8{1'b1}}), .lt(comparator_2_lt));  // open: gt, eq
  LED halted_led (.in(halted));
  LED clk_led (.in(clk));
  Hex_Digit_Display PC_0 (.value(PC[3:0]));  // open: dp
  Multiplexer #(.enable("false"), .select(2), .width(16)) multiplexer_3 (
    .in0({H, L}), .in1({C0, C1}), .in2(adder_1_out), .out(multiplexer_3_out), .sel(mode[1:0]));  // open: in3
  not not_1 (not_1_out, multiplexer_2_out);
  Multiplexer #(.enable("false"), .select(2)) multiplexer_4 (
    .in0(multiplexer_2_out), .in1(not_1_out), .in2(comparator_1_gt), .in3(comparator_2_lt),
    .out(multiplexer_4_out), .sel(mode[1:0]));
  Hex_Digit_Display PC_1 (.value(PC[7:4]));  // open: dp
  Hex_Digit_Display PC_2 (.value(PC[11:8]));  // open: dp
  assign bit_extender_1_out = {{8{data[7]}}, data};  // Bit_Extender bit_extender_1
  Adder #(.width(16)) adder_1 (.a(bit_extender_1_out), .b(PC), .out(adder_1_out));  // open: cin, cout
  Adder #(.width(16)) adder_2 (.a(PC), .b(16'h1), .out(adder_2_out));  // open: cin, cout
  and and_1 (and_1_out, cond_en, multiplexer_4_out);
  Comparator #(.width(3)) comparator_3 (
    .a(instr_state), .b(3'b001), .eq(comparator_3_eq), .lt(comparator_3_lt));  // open: gt
  Button clk_btn (.out(clk_btn_out));
  Clock clock_1 (.out(clk));
  Hex_Digit_Display PC_3 (.value(PC[15:12]));  // open: dp
  Register u_Instr (.D(mem), .en(comparator_4_eq), .clk(clk), .Q(Instr_q));  // open: clr
  Register #(.width(3)) u_Instr_State (.D(multiplexer_5_out), .en(1'b1), .clk(clk), .Q(instr_state));  // open: clr
  Multiplexer #(.enable("false"), .width(3)) multiplexer_5 (
    .in0(multiplexer_6_out), .in1(instr_state), .out(multiplexer_5_out), .sel(or_2_out));
  or or_2 (or_2_out, freeze, halted);
  Multiplexer #(.enable("false"), .width(3)) multiplexer_6 (
    .in0(adder_3_out), .in1(3'b000), .out(multiplexer_6_out), .sel(or_3_out));
  Register #(.width(1)) u_Halted (.D(1'b1), .en(and_2_out), .clk(clk), .Q(halted), .clr(comparator_3_lt));
  and and_2 (and_2_out, halt, comparator_3_eq);
  Hex_Digit_Display A_0 (.value(A[3:0]));  // open: dp
  Hex_Digit_Display A_1 (.value(A[7:4]));  // open: dp
  not not_2 (not_2_out, comparator_4_eq);
  or or_3 (or_3_out, and_1_out, Microcode_data[22]);
  Hex_Digit_Display B_0 (.value(B[3:0]));  // open: dp
  // Probe on {instr, cond}
  Multiplexer #(.enable("false"), .width(8)) multiplexer_7 (
    .in0(mem), .in1(Instr_q), .out({instr, cond}), .sel(not_2_out));
  Comparator #(.width(3)) comparator_4 (.a(instr_state), .b(3'b000), .eq(comparator_4_eq));  // open: gt, lt
  Adder #(.width(3)) adder_3 (.a(instr_state), .b(3'b001), .out(adder_3_out));  // open: cin, cout
  Hex_Digit_Display B_1 (.value(B[7:4]));  // open: dp
  assign bit_extender_2_out = {{1{1'b0}}, shifter_1_out};  // Bit_Extender bit_extender_2
  Shifter #(.shift("lr")) shifter_1 (.in({instr, cond}), .\dist (3'b010), .out(shifter_1_out));
  assign bit_extender_3_out = {{6{1'b0}}, instr_state};  // Bit_Extender bit_extender_3
  LED LED_9 (.in(leds[9]));
  Hex_Digit_Display instr_0 (.value({instr[3:2], cond}));  // open: dp
  Multiplier #(.width(9)) multiplier_1 (
    .a(bit_extender_2_out), .b(9'h6), .out(multiplier_1_out), .cin(bit_extender_3_out));  // open: cout
  Register #(.width(4)) u_F (.D(F_val), .en(F_write), .clk(clk), .Q(F));  // open: clr
  LED LED_8 (.in(leds[8]));
  LED LED_7 (.in(leds[7]));
  LED LED_6 (.in(leds[6]));
  LED LED_5 (.in(leds[5]));
  Button Button_1 (.out(btn0));
  Button Button_2 (.out(btn1));
  Hex_Digit_Display instr_1 (.value(instr[7:4]));  // open: dp
  ROM #(.addrWidth(9), .dataWidth(24)) Microcode (
    .addr(multiplier_1_out),
    .data({Microcode_data[23:20], halt, cond_en, F_write, write, SP_inc, SP_en, mode, write_sel, read_sel, write_op_sel, Microcode_data[1:0]}));
  // Probe on F
  LED LED_4 (.in(leds[4]));
  LED LED_3 (.in(leds[3]));
  LED LED_2 (.in(leds[2]));
  LED LED_1 (.in(leds[1]));
  LED LED_0 (.in(leds[0]));
  Hex_Digit_Display instruction_state (.value(bit_extender_4_out));  // open: dp
  assign bit_extender_4_out = {{1{1'b0}}, instr_state};  // Bit_Extender bit_extender_4
  Register u_SP (.D(multiplexer_8_out), .en(SP_en), .clk(clk), .Q(SP));  // open: clr
  // DipSwitch #(.number(10)) DipSwitch_1: pin names not known; wires that end beside it: switches[0], switches[1], switches[2], switches[3], switches[4], switches[5], switches[6], switches[7], switches[8], switches[9]
  Hex_Digit_Display C0_0 (.value(C0[3:0]));  // open: dp
  // Probe on cond
  Hex_Digit_Display HEX5 (.value(seven_seg[23:20]));  // open: dp
  Hex_Digit_Display C0_1 (.value(C0[7:4]));  // open: dp
  Adder adder_4 (.a(SP), .b(8'h1), .out(adder_4_out));  // open: cin, cout
  Multiplexer #(.enable("false"), .width(8)) multiplexer_8 (
    .in0(adder_4_out), .in1(subtractor_1_out), .out(multiplexer_8_out), .sel(SP_inc));
  Subtractor subtractor_1 (.a(SP), .b(8'h1), .out(subtractor_1_out));  // open: bin, bout
  Hex_Digit_Display HEX4 (.value(seven_seg[19:16]));  // open: dp
  Hex_Digit_Display HEX3 (.value(seven_seg[15:12]));  // open: dp
  Hex_Digit_Display C1_0 (.value(C1[3:0]));  // open: dp
  // Probe on Microcode_data[1:0]
  Multiplexer #(.enable("false"), .width(2)) multiplexer_9 (
    .in0(Microcode_data[1:0]), .in1(2'b00), .out(addr_mode), .sel(comparator_4_eq));
  // Probe on write_op_sel
  // Probe on read_sel
  // Probe on write_sel
  // Probe on mode
  Hex_Digit_Display HEX2 (.value(seven_seg[11:8]));  // open: dp
  Hex_Digit_Display HEX1 (.value(seven_seg[7:4]));  // open: dp
  // PortIO #(.number(2)) clocks_port: pin names not known; wires that end beside it: 1'b0, 2'b00, {clocks_port_p3[1], DE10_clk}
  Hex_Digit_Display C1_1 (.value(C1[7:4]));  // open: dp
  Hex_Digit_Display HEX0 (.value(seven_seg[3:0]));  // open: dp
  Hex_Digit_Display gfx_x0 (.value(gfx_x[3:0]));  // open: dp
  Hex_Digit_Display gfx_x1 (.value(gfx_x[7:4]));  // open: dp
  ADC_dummy adc_dummy_1 (.adc_clk(clk), .ch0(adc_0), .ch1(adc_1), .ch2(adc_2), .ch3(adc_3), .ch4(adc_4), .ch5(adc_5));
  Hex_Digit_Display gfx_y0 (.value(gfx_y[3:0]));  // open: dp
  Hex_Digit_Display adc0 (.value(adc_0[3:0]));  // open: dp
  Hex_Digit_Display gfx_y1 (.value(gfx_y[7:4]));  // open: dp
  Hex_Digit_Display adc1 (.value(adc_0[7:4]));  // open: dp
  // Probe on C0
  Decoder #(.select(2)) decoder_1 (
    .out0(decoder_1_out0), .out1(decoder_1_out1), .out2(decoder_1_out2), .out3(decoder_1_out3),
    .sel(C0[6:5]), .en(port_write));
  Decoder #(.select(5)) decoder_2 (
    .out0(tty_en), .out1(decoder_2_out1), .out2(decoder_2_out2), .out3(decoder_2_out3),
    .out4(decoder_2_out4), .out5(decoder_2_out5), .out6(decoder_2_out6), .out7(decoder_2_out7),
    .out10(decoder_2_out10), .out11(decoder_2_out11), .out12(decoder_2_out12), .out13(decoder_2_out13),
    .out14(decoder_2_out14), .out15(decoder_2_out15), .out16(decoder_2_out16), .out17(decoder_2_out17),
    .out18(decoder_2_out18), .out19(decoder_2_out19), .out30(decoder_2_out30), .out31(decoder_2_out31),
    .sel(C0[4:0]), .en(decoder_1_out0));  // open: out8, out9, out20, out21, out22, out23, out24, out25, out26, out27, out28, out29
  Decoder #(.select(5)) decoder_3 (
    .out0(draw_pixel), .out1(draw_sprite), .out2(clear_screen), .out3(decoder_3_out3), .out4(decoder_3_out4),
    .out5(decoder_3_out5), .out6(decoder_3_out6), .out7(decoder_3_out7), .out8(decoder_3_out8),
    .out9(decoder_3_out9), .out10(decoder_3_out10), .out11(decoder_3_out11), .out12(decoder_3_out12),
    .out13(decoder_3_out13), .out14(decoder_3_out14), .out15(decoder_3_out15), .out16(decoder_3_out16),
    .out17(decoder_3_out17), .out18(decoder_3_out18), .out19(decoder_3_out19), .out20(decoder_3_out20),
    .out21(decoder_3_out21), .out22(decoder_3_out22), .out23(decoder_3_out23), .out24(decoder_3_out24),
    .out25(decoder_3_out25), .out26(decoder_3_out26), .out27(decoder_3_out27), .out28(decoder_3_out28),
    .out29(decoder_3_out29), .out30(decoder_3_out30), .out31(decoder_3_out31), .sel(C0[4:0]),
    .en(decoder_1_out1));
  Decoder #(.select(5)) decoder_4 (
    .out0(decoder_4_out0), .out1(decoder_4_out1), .out2(decoder_4_out2), .out3(decoder_4_out3),
    .out4(decoder_4_out4), .out5(decoder_4_out5), .out6(decoder_4_out6), .out7(decoder_4_out7),
    .out8(decoder_4_out8), .out9(decoder_4_out9), .out10(decoder_4_out10), .out11(decoder_4_out11),
    .out12(decoder_4_out12), .out13(decoder_4_out13), .out14(decoder_4_out14), .out15(decoder_4_out15),
    .out16(decoder_4_out16), .out17(decoder_4_out17), .out18(decoder_4_out18), .out19(decoder_4_out19),
    .out20(decoder_4_out20), .out21(decoder_4_out21), .out22(decoder_4_out22), .out30(decoder_4_out30),
    .out31(decoder_4_out31), .sel(C0[4:0]), .en(decoder_1_out2));  // open: out23, out24, out25, out26, out27, out28, out29
  Decoder #(.select(5)) decoder_5 (
    .out0(decoder_5_out0), .out1(decoder_5_out1), .out2(decoder_5_out2), .sel(C0[4:0]), .en(decoder_1_out3));  // open: out3, out4, out5, out6, out7, out8, out9, out10, out11, out12, out13, out14, out15, out16, out17, out18, out19, out20, out21, out22, out23, out24, out25, out26, out27, out28, out29, out30, out31
  Priority_Encoder #(.select(4)) priority_encoder_1 (
    .in0(decoder_2_out10), .in1(decoder_2_out11), .in2(decoder_2_out12), .in3(decoder_2_out13),
    .in4(decoder_2_out14), .in5(decoder_2_out15), .in6(decoder_2_out16), .in7(decoder_2_out17),
    .in8(decoder_2_out18), .in9(decoder_2_out19), .out(priority_encoder_1_out), .gs(priority_encoder_1_gs),
    .en_in(1'b1));  // open: in10, in11, in12, in13, in14, in15, en_out
  Comparator #(.mode("unsigned")) comparator_5 (.a(data), .b({8{1'b0}}), .gt(comparator_5_gt));  // open: eq, lt
  or or_4 (or_4_out, decoder_3_out3, decoder_3_out4, decoder_3_out5, decoder_3_out6, decoder_3_out7, decoder_3_out8, decoder_3_out9, decoder_3_out10, decoder_3_out11, decoder_3_out12, decoder_3_out13, decoder_3_out14, decoder_3_out15, decoder_3_out16, decoder_3_out17, decoder_3_out18, decoder_3_out19, decoder_3_out20, decoder_3_out21, decoder_3_out22, decoder_3_out23, decoder_3_out24, decoder_3_out25, decoder_3_out26, decoder_3_out27, decoder_3_out28, decoder_3_out29, decoder_3_out30, decoder_3_out31, decoder_4_out0, decoder_4_out1, decoder_4_out2, decoder_4_out3, decoder_4_out4, decoder_4_out5, decoder_4_out6);
  Priority_Encoder #(.select(4)) priority_encoder_2 (
    .in0(decoder_4_out7), .in1(decoder_4_out8), .in2(decoder_4_out9), .in3(decoder_4_out10),
    .in4(decoder_4_out11), .in5(decoder_4_out12), .in6(decoder_4_out13), .in7(decoder_4_out14),
    .in8(decoder_4_out15), .in9(decoder_4_out16), .in10(decoder_4_out17), .in11(decoder_4_out18),
    .in12(decoder_4_out19), .in13(decoder_4_out20), .in14(decoder_4_out21), .in15(decoder_4_out22),
    .out(priority_encoder_2_out), .gs(priority_encoder_2_gs));  // open: en_out, en_in
  or or_5 (or_5_out, decoder_4_out31, decoder_5_out0);
  or or_6 (or_6_out, decoder_5_out1, decoder_5_out2);
  Register #(.width(4)) register_1 (.D(data[3:0]), .en(decoder_2_out2), .clk(clk), .Q(seven_seg[3:0]));  // open: clr
  assign bit_extender_5_out = {{9{1'b0}}, comparator_5_gt};  // Bit_Extender bit_extender_5
  assign bit_extender_6_out = {{8{1'b0}}, data};  // Bit_Extender bit_extender_6
  Register #(.width(7)) pixel (.D(multiplexer_10_out), .en(draw_sprite), .clk(clk), .Q(pixel_q));  // open: clr
  Multiplexer #(.enable("false"), .width(7)) multiplexer_10 (
    .in0(adder_6_out), .in1({7{1'b0}}), .out(multiplexer_10_out), .sel(comparator_9_eq));
  Decoder #(.select(3)) decoder_6 (
    .out0(decoder_6_out0), .out1(decoder_6_out1), .out2(decoder_6_out2), .out3(decoder_6_out3),
    .out4(decoder_6_out4), .out5(decoder_6_out5), .out6(mem_write), .out7(port_write), .sel(write_sel),
    .en(write));
  Register #(.width(4)) register_2 (.D(data[3:0]), .en(decoder_2_out3), .clk(clk), .Q(seven_seg[7:4]));  // open: clr
  assign not_3_out = ~shifter_2_out;  // NOT_Gate not_3, 10 bits wide
  Shifter #(.width(10)) shifter_2 (.in(10'h1), .\dist (priority_encoder_1_out), .out(shifter_2_out));
  Shifter #(.width(10)) shifter_3 (.in(bit_extender_5_out), .\dist (priority_encoder_1_out), .out(shifter_3_out));
  assign or_7_out = shifter_3_out | and_3_out;  // OR_Gate or_7, 10 bits wide
  assign and_3_out = not_3_out & leds;  // AND_Gate and_3, 10 bits wide
  Bit_Extender #(.out_width(6), .\type ("zero")) bit_extender_7 (.in(subtractor_2_out), .out(bit_extender_7_out));
  Subtractor subtractor_2 (.a(C0), .b(8'h23), .out(subtractor_2_out));  // open: bin, bout
  assign bit_extender_8_out = {{35{1'b0}}, comparator_6_gt};  // Bit_Extender bit_extender_8
  Comparator #(.mode("unsigned")) comparator_6 (.a(data), .b({8{1'b0}}), .gt(comparator_6_gt));  // open: eq, lt
  Bit_Extender #(.out_width(6), .\type ("zero")) bit_extender_9 (.in(data), .out(bit_extender_9_out));
  assign bit_extender_10_out = {{35{1'b0}}, decoder_4_out31};  // Bit_Extender bit_extender_10
  Comparator #(.mode("unsigned")) comparator_7 (.a(data), .b({8{1'b0}}), .gt(comparator_7_gt));  // open: eq, lt
  Bit_Extender #(.out_width(4), .\type ("zero")) bit_extender_11 (.in(data), .out(bit_extender_11_out));
  assign bit_extender_12_out = {{15{1'b0}}, decoder_5_out1};  // Bit_Extender bit_extender_12
  Multiplier #(.width(16)) multiplier_2 (
    .a(bit_extender_6_out), .b(16'h40), .out(multiplier_2_out));  // open: cin, cout
  Adder #(.width(16)) adder_5 (.a(multiplier_2_out), .b(bit_extender_13_out), .out(adder_5_out));  // open: cin, cout
  assign bit_extender_13_out = {{9{1'b0}}, pixel_q};  // Bit_Extender bit_extender_13
  Adder #(.width(7)) adder_6 (.a(pixel_q), .b(7'b0000001), .out(adder_6_out));  // open: cin, cout
  Decoder #(.select(2)) decoder_7 (
    .out0(decoder_7_out0), .out1(decoder_7_out1), .out2(decoder_7_out2), .out3(decoder_7_out3), .sel(cond),
    .en(decoder_6_out1));
  Register #(.width(4)) register_3 (.D(data[3:0]), .en(decoder_2_out4), .clk(clk), .Q(seven_seg[11:8]));  // open: clr
  Register #(.width(10)) u_LEDs (.D(or_7_out), .en(priority_encoder_1_gs), .clk(clk), .Q(leds));  // open: clr
  Shifter #(.width(36)) shifter_4 (.in(36'h1), .\dist (bit_extender_7_out), .out(shifter_4_out));
  Shifter #(.width(36)) shifter_5 (.in(bit_extender_8_out), .\dist (bit_extender_7_out), .out(shifter_5_out));
  Shifter #(.width(36)) shifter_6 (.in(36'h1), .\dist (bit_extender_9_out), .out(shifter_6_out));
  Shifter #(.width(36)) shifter_7 (.in(bit_extender_10_out), .\dist (bit_extender_9_out), .out(shifter_7_out));
  assign and_4_out = not_4_out & GPIO_mode_q;  // AND_Gate and_4, 36 bits wide
  Shifter #(.width(16)) shifter_8 (.in(16'h1), .\dist (priority_encoder_2_out), .out(shifter_8_out));
  assign bit_extender_14_out = {{15{1'b0}}, comparator_7_gt};  // Bit_Extender bit_extender_14
  Shifter #(.width(16)) shifter_9 (.in(bit_extender_14_out), .\dist (priority_encoder_2_out), .out(shifter_9_out));
  Shifter #(.width(16)) shifter_10 (.in(16'h1), .\dist (bit_extender_11_out), .out(shifter_10_out));
  Shifter #(.width(16)) shifter_11 (.in(bit_extender_12_out), .\dist (bit_extender_11_out), .out(shifter_11_out));
  assign and_5_out = not_5_out & Arduino_mode_q;  // AND_Gate and_5, 16 bits wide
  Adder #(.width(16)) adder_7 (.a({16{1'b0}}), .b(adder_5_out), .out(addr_override));  // open: cin, cout
  Comparator #(.mode("unsigned"), .width(7)) comparator_8 (
    .a(pixel_q), .b({7{1'b0}}), .gt(comparator_8_gt));  // open: eq, lt
  Comparator #(.mode("unsigned"), .width(7)) comparator_9 (
    .a(pixel_q), .b(7'b1000000), .eq(comparator_9_eq), .lt(comparator_9_lt));  // open: gt
  Register u_A (.D(data), .en(or_8_out), .clk(clk), .Q(A));  // open: clr
  or or_8 (or_8_out, decoder_6_out0, decoder_7_out0);
  Register u_B (.D(data), .en(decoder_7_out1), .clk(clk), .Q(B));  // open: clr
  Register u_H (.D(data), .en(or_9_out), .clk(clk), .Q(H));  // open: clr
  or or_9 (or_9_out, decoder_7_out2, decoder_6_out2);
  Register u_L (.D(data), .en(or_10_out), .clk(clk), .Q(L));  // open: clr
  or or_10 (or_10_out, decoder_7_out3, decoder_6_out3);
  Register u_C0 (.D(data), .en(decoder_6_out4), .clk(clk), .Q(C0));  // open: clr
  Register u_C1 (.D(data), .en(decoder_6_out5), .clk(clk), .Q(C1));  // open: clr
  Register #(.width(4)) register_4 (.D(data[3:0]), .en(decoder_2_out5), .clk(clk), .Q(seven_seg[15:12]));  // open: clr
  assign and_6_out = not_6_out & GPIO_out_q;  // AND_Gate and_6, 36 bits wide
  Register #(.width(36)) GPIO_out (.D(or_11_out), .en(or_4_out), .clk(clk), .Q(GPIO_out_q));  // open: clr
  assign or_11_out = and_6_out | shifter_5_out;  // OR_Gate or_11, 36 bits wide
  assign not_4_out = ~shifter_6_out;  // NOT_Gate not_4, 36 bits wide
  Register #(.width(36)) GPIO_mode (.D(or_12_out), .en(or_5_out), .clk(clk), .Q(GPIO_mode_q));  // open: clr
  assign or_12_out = shifter_7_out | and_4_out;  // OR_Gate or_12, 36 bits wide
  Register #(.width(16)) Arduino_out (
    .D(or_13_out), .en(priority_encoder_2_gs), .clk(clk), .Q(Arduino_out_q));  // open: clr
  assign or_13_out = and_9_out | shifter_9_out;  // OR_Gate or_13, 16 bits wide
  assign not_5_out = ~shifter_10_out;  // NOT_Gate not_5, 16 bits wide
  Register #(.width(16)) Arduino_mode (.D(or_14_out), .en(or_6_out), .clk(clk), .Q(Arduino_mode_q));  // open: clr
  assign or_14_out = shifter_11_out | and_5_out;  // OR_Gate or_14, 16 bits wide
  and and_7 (addr_override_en, comparator_9_lt, draw_sprite);
  and and_8 (and_8_out, comparator_9_lt, comparator_8_gt);
  assign mem_val = mem_write ? data : 8'bz;  // Controlled_Buffer controlled_buffer_1
  Register #(.width(4)) register_5 (.D(data[3:0]), .en(decoder_2_out6), .clk(clk), .Q(seven_seg[19:16]));  // open: clr
  assign not_6_out = ~shifter_4_out;  // NOT_Gate not_6, 36 bits wide
  // PortIO #(.direction("IOMultiEnable"), .number(36)) GPIO_port: pin names not known; wires that end beside it: GPIO_mode_q, GPIO_out_q, GPIO_in
  assign not_7_out = ~shifter_8_out;  // NOT_Gate not_7, 16 bits wide
  assign and_9_out = not_7_out & Arduino_out_q;  // AND_Gate and_9, 16 bits wide
  // PortIO #(.direction("IOMultiEnable"), .number(16)) Arduino_port: pin names not known; wires that end beside it: Arduino_mode_q, Arduino_out_q, Arduino_in
  Subtractor #(.width(7)) subtractor_3 (.a(pixel_q), .b({7{1'b0}}), .out(subtractor_3_out));  // open: bin, bout
  or or_15 (or_15_out, and_8_out, draw_pixel);
  Multiplexer #(.enable("false"), .select(2), .width(8)) multiplexer_11 (
    .in0(A), .in1(B), .in2(H), .in3(L), .out(multiplexer_11_out), .sel(cond));
  Register #(.width(4)) register_6 (.D(data[3:0]), .en(decoder_2_out7), .clk(clk), .Q(seven_seg[23:20]));  // open: clr
  Register graphics_x (.D(data), .en(decoder_2_out30), .clk(clk), .Q(gfx_x));  // open: clr
  assign bit_extender_15_out = {{5{1'b0}}, subtractor_3_out[2:0]};  // Bit_Extender bit_extender_15
  assign bit_extender_16_out = {{5{1'b0}}, subtractor_3_out[5:3]};  // Bit_Extender bit_extender_16
  Multiplexer #(.enable("false"), .select(4), .width(8)) multiplexer_12 (
    .in0(A), .in1(multiplexer_11_out), .in2(H), .in3(L), .in4(C0), .in5(C1), .in6(mem), .in7(PC[7:0]),
    .in8(PC[15:8]), .in9(port_in), .in10(8'hee), .in11(8'hee), .in12(8'hee), .in13(8'hee), .in14(8'hee),
    .in15(8'hee), .out(multiplexer_12_out), .sel(read_sel));
  // Probe on multiplexer_12_out
  Register graphics_y (.D(data), .en(decoder_2_out31), .clk(clk), .Q(gfx_y));  // open: clr
  Multiplexer #(.enable("false"), .width(8)) multiplexer_13 (
    .in0(data), .in1(mem), .out(multiplexer_13_out), .sel(draw_sprite));
  Multiplexer #(.enable("false"), .width(8)) multiplexer_14 (
    .in0(gfx_x), .in1(adder_8_out), .out(multiplexer_14_out), .sel(draw_sprite));
  Adder adder_8 (.a(gfx_x), .b(bit_extender_15_out), .out(adder_8_out));  // open: cin, cout
  Multiplexer #(.enable("false"), .width(8)) multiplexer_15 (
    .in0(gfx_y), .in1(adder_9_out), .out(multiplexer_15_out), .sel(draw_sprite));
  Adder adder_9 (.a(gfx_y), .b(bit_extender_16_out), .out(adder_9_out));  // open: cin, cout
  Adder adder_10 (.a(multiplexer_12_out), .b(8'h1), .out(adder_10_out), .cout(adder_10_cout[2]));  // open: cin
  Subtractor subtractor_4 (
    .a(multiplexer_12_out), .b(8'h1), .out(subtractor_4_out), .bout(subtractor_4_bout[2]));  // open: bin
  alu alu_1 (
    .mode(mode), .A(A), .operand(multiplexer_12_out), .flags_in(F), .result(alu_1_result),
    .flags_out(alu_1_flags_out));
  Comparator #(.mode("unsigned")) comparator_10 (.a(data), .b({8{1'b0}}), .eq(adder_10_cout[3]));  // open: gt, lt
  buf or_16 (freeze, addr_override_en);  // OR_Gate
  VGA_driver vga_driver_1 (
    .clk(DE10_clk), .color_in(multiplexer_13_out), .x_in(multiplexer_14_out), .y_in(multiplexer_15_out),
    .write_clk(clk), .WE(or_15_out), .HS(vga_driver_1_hs[0]), .VS(vga_driver_1_hs[1]),
    .vga_r(vga_driver_1_vga_r), .vga_g(vga_driver_1_vga_g), .vga_b(vga_driver_1_vga_b));
  // PortIO #(.number(14)) VGA_port: pin names not known; wires that end beside it: 1'b1, {vga_driver_1_vga_b, vga_driver_1_vga_g, vga_driver_1_vga_r, vga_driver_1_hs}, VGA_port_p3, VGA_port_p3
  Multiplexer #(.enable("false"), .select(2), .width(4)) multiplexer_16 (
    .in0(alu_1_flags_out), .in1(multiplexer_18_out), .in2({adder_10_cout, F[1:0]}),
    .in3({adder_10_cout[3], subtractor_4_bout[2], F[1:0]}), .out(F_val), .sel(write_op_sel));
  Multiplexer #(.enable("false"), .select(2), .width(8)) multiplexer_17 (
    .in0(alu_1_result), .in1(multiplexer_12_out), .in2(adder_10_out), .in3(subtractor_4_out), .out(data),
    .sel(write_op_sel));
  Negator negator_1 (.in(SP), .out(negator_1_out));
  Comparator comparator_11 (.a(data), .b({8{1'b0}}), .eq(comparator_11_eq));  // open: gt, lt
  // Probe on data
  assign bit_extender_17_out = {{8{1'b1}}, negator_1_out};  // Bit_Extender bit_extender_17
  Comparator #(.mode("unsigned"), .width(16)) comparator_12 (
    .a(PC), .b({16{1'b0}}), .gt(comparator_12_gt));  // open: eq, lt
  assign and_10_out = F & 4'b0111;  // AND_Gate and_10, 4 bits wide
  Multiplexer #(.enable("false"), .width(4)) multiplexer_18 (
    .in0(and_10_out), .in1(or_17_out), .out(multiplexer_18_out), .sel(comparator_11_eq));
  assign or_17_out = F | 4'b1000;  // OR_Gate or_17, 4 bits wide
  Multiplexer #(.enable("false"), .select(2), .width(16)) multiplexer_19 (
    .in0(PC), .in1(bit_extender_17_out), .in2({H, L}), .in3({C0, C1}), .out(multiplexer_19_out),
    .sel(addr_mode));
  Multiplexer #(.enable("false"), .width(16)) multiplexer_20 (
    .in0(multiplexer_19_out), .in1(addr_override), .out(multiplexer_20_out), .sel(and_11_out));
  and and_11 (and_11_out, addr_override_en, comparator_12_gt);
  // Probe on multiplexer_20_out
  RAM #(.addrWidth(15)) RAM_1 (
    .addr(multiplexer_20_out[14:0]), .we(mem_write), .oe(1'b1), .clk(clk), .din(mem_val), .dout(RAM_1_dout));
  Subtractor #(.width(5)) subtractor_5 (.a(C0[4:0]), .b(5'b00010), .out(subtractor_5_out));  // open: bin, bout
  Subtractor #(.width(5)) subtractor_6 (.a(C0[4:0]), .b(5'b01010), .out(subtractor_6_out));  // open: bin, bout
  Subtractor #(.width(5)) subtractor_7 (.a(C0[4:0]), .b(5'b10100), .out(subtractor_7_out));  // open: bin, bout
  Subtractor subtractor_8 (.a(C0), .b(8'h23), .out(subtractor_8_out));  // open: bin, bout
  Subtractor #(.width(5)) subtractor_9 (.a(C0[4:0]), .b(5'b01000), .out(subtractor_9_out));  // open: bin, bout
  Random random_1 (.next(1'b1), .clk(clock_2_out), .out(random_1_out));  // open: clr
  Clock clock_2 (.out(clock_2_out));
  assign bit_extender_18_out = {{4{1'b0}}, multiplexer_21_out};  // Bit_Extender bit_extender_18
  Multiplexer #(.enable("false"), .select(3), .width(4)) multiplexer_21 (
    .in0(seven_seg[3:0]), .in1(seven_seg[7:4]), .in2(seven_seg[11:8]), .in3(seven_seg[15:12]),
    .in4(seven_seg[19:16]), .in5(seven_seg[23:20]), .out(multiplexer_21_out), .sel(subtractor_5_out[2:0]));  // open: in6, in7
  Shifter #(.width(10)) shifter_12 (.in(10'h1), .\dist (subtractor_6_out[3:0]), .out(shifter_12_out));
  Shifter #(.width(10)) shifter_13 (.in(10'h1), .\dist (subtractor_7_out[3:0]), .out(shifter_13_out));
  Shifter #(.width(36)) shifter_14 (.in(36'h1), .\dist (subtractor_8_out[5:0]), .out(shifter_14_out));
  Shifter #(.width(16)) shifter_15 (.in(16'h1), .\dist (subtractor_9_out[3:0]), .out(shifter_15_out));
  ROM #(.addrWidth(15)) Program (.addr(multiplexer_20_out[14:0]), .data(Program_data));
  assign and_12_out = shifter_12_out & leds;  // AND_Gate and_12, 10 bits wide
  Comparator #(.mode("unsigned"), .width(10)) comparator_13 (
    .a(and_12_out), .b({10{1'b0}}), .gt(comparator_13_gt));  // open: eq, lt
  assign and_13_out = shifter_13_out & switches;  // AND_Gate and_13, 10 bits wide
  Comparator #(.mode("unsigned"), .width(10)) comparator_14 (
    .a(and_13_out), .b({10{1'b0}}), .gt(comparator_14_gt));  // open: eq, lt
  assign and_14_out = shifter_14_out & GPIO_in;  // AND_Gate and_14, 36 bits wide
  Comparator #(.mode("unsigned"), .width(36)) comparator_15 (
    .a(and_14_out), .b({36{1'b0}}), .gt(comparator_15_gt));  // open: eq, lt
  assign and_15_out = shifter_15_out & Arduino_in;  // AND_Gate and_15, 16 bits wide
  Comparator #(.mode("unsigned"), .width(16)) comparator_16 (
    .a(and_15_out), .b({16{1'b0}}), .gt(comparator_16_gt));  // open: eq, lt
  assign bit_extender_19_out = {{7{1'b0}}, btn0};  // Bit_Extender bit_extender_19
  assign bit_extender_20_out = {{7{1'b0}}, btn1};  // Bit_Extender bit_extender_20
  assign bit_extender_21_out = {{7{1'b0}}, comparator_13_gt};  // Bit_Extender bit_extender_21
  assign bit_extender_22_out = {{7{1'b0}}, comparator_14_gt};  // Bit_Extender bit_extender_22
  assign bit_extender_23_out = {{7{1'b0}}, comparator_15_gt};  // Bit_Extender bit_extender_23
  assign bit_extender_24_out = {{7{1'b0}}, comparator_16_gt};  // Bit_Extender bit_extender_24
  Multiplexer #(.enable("false"), .select(5), .width(8)) multiplexer_22 (
    .in0({8{1'b0}}), .in1({8{1'b0}}), .in2(bit_extender_18_out), .in3(bit_extender_18_out),
    .in4(bit_extender_18_out), .in5(bit_extender_18_out), .in6(bit_extender_18_out),
    .in7(bit_extender_18_out), .in8(bit_extender_19_out), .in9(bit_extender_20_out),
    .in10(bit_extender_21_out), .in11(bit_extender_21_out), .in12(bit_extender_21_out),
    .in13(bit_extender_21_out), .in14(bit_extender_21_out), .in15(bit_extender_21_out),
    .in16(bit_extender_21_out), .in17(bit_extender_21_out), .in18(bit_extender_21_out),
    .in19(bit_extender_21_out), .in20(bit_extender_22_out), .in21(bit_extender_22_out),
    .in22(bit_extender_22_out), .in23(bit_extender_22_out), .in24(bit_extender_22_out),
    .in25(bit_extender_22_out), .in26(bit_extender_22_out), .in27(bit_extender_22_out),
    .in28(bit_extender_22_out), .in29(bit_extender_22_out), .in30(gfx_x), .in31(gfx_y),
    .out(multiplexer_22_out), .sel(C0[4:0]));
  Multiplexer #(.enable("false"), .select(5), .width(8)) multiplexer_23 (
    .in0({8{1'b0}}), .in1({8{1'b0}}), .in2({8{1'b0}}), .in3(bit_extender_23_out), .in4(bit_extender_23_out),
    .in5(bit_extender_23_out), .in6(bit_extender_23_out), .in7(bit_extender_23_out),
    .in8(bit_extender_23_out), .in9(bit_extender_23_out), .in10(bit_extender_23_out),
    .in11(bit_extender_23_out), .in12(bit_extender_23_out), .in13(bit_extender_23_out),
    .in14(bit_extender_23_out), .in15(bit_extender_23_out), .in16(bit_extender_23_out),
    .in17(bit_extender_23_out), .in18(bit_extender_23_out), .in19(bit_extender_23_out),
    .in20(bit_extender_23_out), .in21(bit_extender_23_out), .in22(bit_extender_23_out),
    .in23(bit_extender_23_out), .in24(bit_extender_23_out), .in25(bit_extender_23_out),
    .in26(bit_extender_23_out), .in27(bit_extender_23_out), .in28(bit_extender_23_out),
    .in29(bit_extender_23_out), .in30(bit_extender_23_out), .in31(bit_extender_23_out),
    .out(multiplexer_23_out), .sel(C0[4:0]));
  Multiplexer #(.enable("false"), .select(5), .width(8)) multiplexer_24 (
    .in0(bit_extender_23_out), .in1(bit_extender_23_out), .in2(bit_extender_23_out),
    .in3(bit_extender_23_out), .in4(bit_extender_23_out), .in5(bit_extender_23_out),
    .in6(bit_extender_23_out), .in7(bit_extender_24_out), .in8(bit_extender_24_out),
    .in9(bit_extender_24_out), .in10(bit_extender_24_out), .in11(bit_extender_24_out),
    .in12(bit_extender_24_out), .in13(bit_extender_24_out), .in14(bit_extender_24_out),
    .in15(bit_extender_24_out), .in16(bit_extender_24_out), .in17(bit_extender_24_out),
    .in18(bit_extender_24_out), .in19(bit_extender_24_out), .in20(bit_extender_24_out),
    .in21(bit_extender_24_out), .in22(bit_extender_24_out), .in23(adc_0), .in24(adc_1), .in25(adc_2),
    .in26(adc_3), .in27(adc_4), .in28(adc_5), .in29(random_1_out), .in30({8{1'b0}}), .in31({8{1'b0}}),
    .out(multiplexer_24_out), .sel(C0[4:0]));
  // Probe on C0[4:0]
  // Probe on C0[6:5]
  Multiplexer #(.enable("false"), .select(2), .width(8)) multiplexer_25 (
    .in0(multiplexer_22_out), .in1(multiplexer_23_out), .in2(multiplexer_24_out), .in3({8{1'b0}}),
    .out(port_in), .sel(C0[6:5]));
  Multiplexer #(.enable("false"), .width(8)) multiplexer_26 (
    .in0(Program_data), .in1(RAM_1_dout), .out(mem), .sel(multiplexer_20_out[15]));
  // Probe on port_in

  // Other names for the same wires on the sheet: mode_1 = mode[0]; mode_2[1:0] = mode[1:0];
  //   draw_sprite_freeze = addr_override_en; instr[1:0] = cond; reg_sel[1:0] = cond

  // Notes on the sheet:
  //   contents of Microcode (hex, n*v repeats v):
  //   400000 6*0 530164 5*0 110464 110564 3 30167 400000 0 2 430166 4*0 110464 110564 410617 0 0 0 410616
  //   5*0 110264 510364 4*0 110464 430194 4*0 110464 410714 0 0 0 430118 5*0 43011c 5*0 30338 41030 430228
  //   0 0 0 3033c 41834 43022c 4*0 110464 430040 0 0 0 430010 6*0 110464 430840 0 0 0 430810 6*0 110464
  //   431040 0 0 0 431010 6*0 110464 431840 0 0 0 431810 6*0 110464 432040 0 0 0 432010 6*0 110464 432840
  //   0 0 0 432810 6*0 110464 433040 0 0 0 433010 6*0 110464 423840 0 0 0 423810 6*0 110464 110564 600800
  //   0 0 600000 6*0 201064 500000 4*0 110464 40800 601044 0 0 0 110464 40000 601044 0 0 0 10404 430194
  //   4*0 10404 410714 0 0 0 4000 410615 5*0 1 41c165 4*0 110464 114564 14675 10685 600800 0 1 1c465 1
  //   1c565 600800 0 80000
  //   2 pins
  //   36 pins
  //   16 pins
  //   14 pins
  //   contents of Program (hex, n*v repeats v):
  //   4 1 20 2 1c 2 24 20 3 1c 3 24 20 4 1c 4 24 20 5 1c 5 24 20 6 1c 6 24 20 7 4 a 28 5 1 24 8d 90 88 64
  //   1 90 95 94 6c 13 84 f3 4 1 20 5f 20 61 4 0 6 7f 22 1f 7 9f 23 1e 34 8 20 20 2b 85 f7 2a 85 f0 20 5e
  //   1c 23 20 24 1c 15 20 48 1c 8 80 3 98 0 63 1c 9 80 3 98 0 73 7c e8 4 9 34 14 89 44 14 34 a 8d 44 a 28
  //   85 f3 9c 4 9 90 6c 5 85 4 34 23 7c 4 44 4 34 47 89 94 34 a 8d 44 a 28 85 e9 9c
endmodule

module alu (
  input  [2:0] mode,
  input  [7:0] A,
  input  [7:0] operand,
  input  [3:0] flags_in,
  output [7:0] result,
  output [3:0] flags_out
);

  wire adder_1_cout, adder_2_cout, comparator_1_lt, comparator_2_lt, subtractor_1_bout, subtractor_2_bout,
       xnor_1_out, xor_2_out;
  wire [1:0] and_2_out;
  wire [7:0] adder_1_out, adder_2_out, and_1_out, or_1_out, subtractor_1_out, subtractor_2_out, xor_1_out;

  Comparator comparator_1 (.a(A), .b({8{1'b0}}), .lt(comparator_1_lt));  // open: gt, eq
  Comparator comparator_2 (.a(operand), .b({8{1'b0}}), .lt(comparator_2_lt));  // open: gt, eq
  Multiplexer #(.enable("false"), .select(3), .width(2)) multiplexer_1 (
    .in0(and_2_out), .in1(and_2_out), .in2(and_2_out), .in3(and_2_out), .in4(and_2_out), .in5(flags_in[1:0]),
    .in6(flags_in[1:0]), .in7(flags_in[1:0]), .out(flags_out[1:0]), .sel(mode));
  Adder adder_1 (.a(A), .b(operand), .out(adder_1_out), .cout(adder_1_cout));  // open: cin
  Adder adder_2 (.a(A), .b(operand), .out(adder_2_out), .cin(flags_in[2]), .cout(adder_2_cout));
  Subtractor subtractor_1 (.a(A), .b(operand), .out(subtractor_1_out), .bout(subtractor_1_bout));  // open: bin
  Subtractor subtractor_2 (.a(A), .b(operand), .out(subtractor_2_out), .bin(flags_in[2]), .bout(subtractor_2_bout));
  assign and_1_out = A & operand;  // AND_Gate and_1, 8 bits wide
  assign or_1_out = A | operand;  // OR_Gate or_1, 8 bits wide
  assign xor_1_out = A ^ operand;  // XOR_Gate xor_1, 8 bits wide
  xnor xnor_1 (xnor_1_out, comparator_1_lt, comparator_2_lt);
  and and_2 (and_2_out[0], xnor_1_out, xor_2_out);
  Multiplexer #(.enable("false"), .select(3)) multiplexer_2 (
    .in0(adder_1_cout), .in1(adder_2_cout), .in2(subtractor_1_bout), .in3(subtractor_2_bout),
    .in4(flags_in[2]), .in5(flags_in[2]), .in6(flags_in[2]), .in7(subtractor_1_bout), .out(flags_out[2]),
    .sel(mode));
  xor xor_2 (xor_2_out, comparator_2_lt, and_2_out[1]);
  Multiplexer #(.enable("false"), .select(3), .width(8)) multiplexer_3 (
    .in0(adder_1_out), .in1(adder_2_out), .in2(subtractor_1_out), .in3(subtractor_2_out), .in4(and_1_out),
    .in5(or_1_out), .in6(xor_1_out), .in7(subtractor_1_out), .out(result), .sel(mode));
  Comparator comparator_3 (.a(result), .b({8{1'b0}}), .eq(flags_out[3]), .lt(and_2_out[1]));  // open: gt

  // Notes on the sheet:
  //   ADD
  //   ADC
  //   SUB
  //   SBC
  //   AND
  //   OR
  //   XOR
endmodule

// VHDL entity DE10_RAM, as the project stores it:
-- A syncronous RAM component compatible with the DE10-Lite board

library ieee;
use ieee.std_logic_1164.all;

entity DE10_RAM is
	port (
  		WE : in std_logic; -- Write enable
  		clk : in std_logic; -- Clock pin
  		DataIn : in std_logic_vector(7 downto 0); -- Data input
  		Address : in std_logic_vector(14 downto 0); -- Memory address
  		DataOut : out std_logic_vector(7 downto 0) -- Data output
	);
end DE10_RAM;

architecture impl of DE10_RAM is
	type MEMORY_ARRAY is array (32767 downto 0) of std_logic_vector(7 downto 0);
	signal memory : MEMORY_ARRAY;
begin
	process (clk, Address, DataIn, WE)
	begin
     	if (clk'event and (clk = '1')) then
     		if (WE = '1') then
          		memory(to_integer(unsigned(Address))) <= DataIn;
          	end if;
			DataOut <= memory(to_integer(unsigned(Address)));
      	end if;
	end process;
end architecture;

// VHDL entity VGA_driver, as the project stores it:
-- A DE10-Lite VGA driver

library ieee;
use ieee.std_logic_1164.all;
use ieee.numeric_std.all;
use ieee.std_logic_unsigned.all;

entity VGA_driver is
	port (
		clk : in std_logic;
		color_in : in std_logic_vector(7 downto 0); -- Color of pixel to write into VRAM
		x_in, y_in : in std_logic_vector(7 downto 0); -- Coordinates of pixel to write
		write_clk : in std_logic; -- Clock for writing to VRAM
		WE : in std_logic; -- VRAM write enable
		HS, VS : out std_logic; -- VGA horizontal and vertical sync
		vga_r, vga_g, vga_b : out std_logic_vector(3 downto 0) -- VGA output color
	);
end VGA_driver;

architecture TypeArchitecture of VGA_driver is
	type COLOR_ARRAY is array (20479 downto 0) of std_logic_vector(11 downto 0);
	
	signal h_cnt : unsigned(10 downto 0);
	signal v_cnt : unsigned(9 downto 0);
	signal vga_clk : std_logic;
	signal display_buffer : COLOR_ARRAY;
	signal color : std_logic_vector(11 downto 0);
	signal x : unsigned(10 downto 0);
	signal y : unsigned(9 downto 0);
	signal buffer_index : unsigned(19 downto 0);
begin
	
	process(clk)
	begin
		if clk'event and clk='1' then
			vga_clk <= not vga_clk;
		end if;
	end process;

	process(write_clk, WE, color_in, x_in, y_in)
		variable r, g, b : unsigned(11 downto 0);
	begin
		if write_clk'event and write_clk='1' then
			if WE='1' then
				r := shift_left("000000" & unsigned(color_in(7 downto 5)) * 255 / 7, 8);
				g := shift_left("000000" & unsigned(color_in(4 downto 2)) * 255 / 7, 4);
				b := "00000000" & unsigned(color_in(1 downto 0)) * 255 / 3;
				display_buffer(to_integer(unsigned(x_in) + unsigned(y_in) * 160)) <= std_logic_vector(r or g or b);
			end if;
		end if;
	end process;
	
	process(clk, x, y)
		variable data : std_logic_vector(11 downto 0);
	begin
		if clk'event and clk='1' then
			data := display_buffer(to_integer(buffer_index));  -- Don't move under any circumstance, the inferred RAM implementation is extremely tempermental
			if x<=159 and y<=127 then
				color <= data;
			else
				color <= x"000";
			end if;
		end if;
	end process;
	
	process(vga_clk, color)
	begin
		if vga_clk'event and vga_clk='1' then
			if h_cnt<784 and h_cnt>=144 and v_cnt<514 and v_cnt>=11 then
				vga_r <= color(11 downto 8);
				vga_g <= color(7 downto 4);
				vga_b <= color(3 downto 0);
			else
				vga_r <= x"0";
				vga_g <= x"0";
				vga_b <= x"0";
			end if;
			
			if h_cnt=799 then
				h_cnt <= to_unsigned(0, 11);
				if v_cnt=524 then
					v_cnt <= to_unsigned(0, 10);
				else
					v_cnt <= v_cnt + 1;
				end if;
			else
				h_cnt <= h_cnt + 1;
			end if;
			
			if h_cnt<96 then
				HS <= '1';
			else
				HS <= '0';
			end if;
				
			if v_cnt<2 then
				VS <= '1';
			else
				VS <= '0';
			end if;
					
			x <= (h_cnt - 144) / 3;
			y <= (v_cnt - 11) / 3;
			buffer_index <= x + y * 160;
		end if;
	end process;
end TypeArchitecture;

// VHDL entity ADC_dummy, as the project stores it:
-- A placeholder ADC component for DE10-Lite

library ieee;
use ieee.std_logic_1164.all;

entity ADC_dummy is
  port (
	  adc_clk : in std_logic;
	  ch0 : out std_logic_vector(7 downto 0);
	  ch1 : out std_logic_vector(7 downto 0);
	  ch2 : out std_logic_vector(7 downto 0);
	  ch3 : out std_logic_vector(7 downto 0);
	  ch4 : out std_logic_vector(7 downto 0);
	  ch5 : out std_logic_vector(7 downto 0)
    );
end ADC_dummy;

architecture stub of ADC_dummy is
begin
end architecture;
